# Fritzing sketch Circuit (saved by Fritzing 0.9.6b)

parts:
  U1 = ESP32S-HiLetgo [part_number=ESP32S-HiLetgo]
  Part1 = Adafruit NeoTrellis 4x4 [part_number=https://www.adafruit.com/product/3954]
  Part2 = Adafruit NeoTrellis 4x4 [part_number=https://www.adafruit.com/product/3954]

nets:
  VIN: U1.VIN, Part1.VIN, Part2.VIN
  GND: U1.GND, Part1.GND, Part2.GND
  N1: U1.GPIO21, Part1.SDA, Part2.SDA
  N2: U1.GPIO22, Part1.SCL, Part2.SCL
  N3: Part1.INT, Part2.INT

custom parts:
  ESP32S-HiLetgo: HiLetgo ESP-WROOM-32 ESP32 ESP-32S Development Board 2.4GHz Dual-Mode WiFi + Bluetooth Dual Cores Microcontroller The ESP32 integrated with Antenna switches, RF Balun, power amplifiers, low-noise amplifiers, filters, and management modules, and the entire solution occupies the least area of PCB. 2.4 GHz Wi-Fi plus Bluetooth dual-mode chip, with TSMC Ultra-low power consumption 40nm technology,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
